// Logisim project Circuit Interne.circ as structural Verilog
module Modele_1 (
  input  I1,
  input  I2,
  input  I3,
  input  I4,
  output S1,
  output S2,
  output S3,
  output S4
);

  wire and_1_out, and_2_out, and_3_out, and_4_out, and_5_out, and_6_out, and_7_out, and_8_out, and_9_out,
       and_10_out, and_11_out, and_12_out, and_13_out, and_14_out, and_15_out, and_16_out, and_17_out,
       and_18_out, and_19_out, and_20_out, and_21_out, and_22_out, and_23_out, and_24_out, and_25_out,
       and_26_out, and_27_out, not_1_out, not_2_out, not_3_out, not_4_out, not_5_out, not_6_out, not_7_out,
       not_8_out, not_9_out, not_10_out, not_11_out, not_12_out, not_13_out, not_14_out, not_15_out,
       not_16_out, not_17_out, not_18_out, not_19_out, or_1_out, or_2_out, or_3_out, or_4_out, or_5_out,
       or_6_out, or_9_out, or_10_out;

  not not_1 (not_1_out, I1);
  not not_2 (not_2_out, I2);
  not not_3 (not_3_out, I1);
  not not_4 (not_4_out, I4);
  not not_5 (not_5_out, I3);
  not not_6 (not_6_out, I4);
  not not_7 (not_7_out, I1);
  not not_8 (not_8_out, I3);
  not not_9 (not_9_out, I2);
  not not_10 (not_10_out, I3);
  not not_11 (not_11_out, I1);
  not not_12 (not_12_out, I3);
  not not_13 (not_13_out, I1);
  not not_14 (not_14_out, I4);
  not not_15 (not_15_out, I1);
  not not_16 (not_16_out, I1);
  not not_17 (not_17_out, I3);
  not not_18 (not_18_out, I2);
  and and_1 (and_1_out, not_1_out, not_2_out);
  and and_2 (and_2_out, I3, I4);
  and and_3 (and_3_out, not_3_out, not_4_out);
  or or_1 (or_1_out, and_3_out, and_4_out);
  and and_4 (and_4_out, not_5_out, not_6_out);
  and and_5 (and_5_out, not_7_out, I2);
  and and_6 (and_6_out, I1, not_9_out);
  and and_7 (and_7_out, and_6_out, not_10_out);
  and and_8 (and_8_out, I1, I2);
  and and_9 (and_9_out, I3, I4);
  and and_10 (and_10_out, not_11_out, not_12_out);
  and and_11 (and_11_out, not_13_out, I3);
  and and_12 (and_12_out, I2, I3);
  and and_13 (and_13_out, I1, I2);
  and and_14 (and_14_out, not_15_out, I2);
  and and_15 (and_15_out, not_16_out, I2);
  and and_16 (and_16_out, I1, not_17_out);
  and and_17 (and_17_out, I1, not_18_out);
  and and_18 (and_18_out, I1, I3);
  not not_19 (not_19_out, I4);
  or or_2 (or_2_out, or_1_out, and_19_out);
  and and_19 (and_19_out, and_5_out, not_8_out);
  or or_3 (or_3_out, and_7_out, and_20_out);
  and and_20 (and_20_out, and_8_out, and_9_out);
  and and_21 (and_21_out, and_10_out, I4);
  or or_4 (or_4_out, and_21_out, and_22_out);
  and and_22 (and_22_out, and_11_out, not_14_out);
  or or_5 (or_5_out, and_12_out, and_13_out);
  and and_23 (and_23_out, and_14_out, I4);
  or or_6 (or_6_out, and_23_out, and_24_out);
  and and_24 (and_24_out, and_15_out, I3);
  and and_25 (and_25_out, and_16_out, I4);
  and and_26 (and_26_out, and_17_out, I3);
  and and_27 (and_27_out, and_18_out, not_19_out);
  and and_28 (S1, and_1_out, and_2_out);
  or or_7 (S2, or_2_out, or_3_out);
  or or_8 (S3, or_4_out, or_5_out);
  or or_9 (or_9_out, or_6_out, and_25_out);
  or or_10 (or_10_out, and_26_out, and_27_out);
  or or_11 (S4, or_9_out, or_10_out);
endmodule
