// Logisim project Carte 1011.circ as structural Verilog: 1 circuit, main circuit main
module main (
  input  in_1,
  input  in_2,
  input  in_3,
  input  in_4,
  output out_5,
  output out_6,
  output out_7,
  output out_8
);

  wire and_1_out, and_2_out, not_1_out, not_2_out;

  not not_1 (not_1_out, in_2);
  not not_2 (not_2_out, in_1);
  and and_1 (and_1_out, in_1, not_1_out, not_1_out);
  and and_2 (and_2_out, in_3, in_4);
  and and_3 (out_5, in_1, not_2_out);
  and and_4 (out_8, and_1_out, and_2_out);

  assign out_6 = out_5;
  assign out_7 = out_5;
endmodule
